// Logisim project FullAdderandHalfAdder (1) (1).circ as structural Verilog: 1 circuit, main circuit main
module main (
  input  A,
  input  C,
  input  B,
  input  in_4,
  input  in_5,
  output out_6,
  output out_7,
  output out_8,
  output out_9
);

  wire and_1_out, and_3_out, xor_1_out;

  xor xor_1 (xor_1_out, A, B);
  and and_1 (and_1_out, A, B);
  xor xor_2 (out_8, in_4, in_5);
  and and_2 (out_9, in_4, in_5);
  xor xor_3 (out_6, xor_1_out, C);
  and and_3 (and_3_out, xor_1_out, C);
  or or_1 (out_7, and_3_out, and_1_out);
endmodule
